# Fritzing sketch Infa-red remote control (saved by Fritzing 0.9.6b)
breadboards: 1

parts:
  R1 = Resistor [tolerance=±20% resistance=22k package=THT]
  R2 = Resistor [tolerance=±5% power=0.25 resistance=1M package=THT]
  C1 = Capacitor [package=cap-pth-large]
  S1 = SWITCH-MOMENTARY-2 [package=reed_switch_pth]
  Q1 = TRANSISTOR_PNP [part_number=2N2907 package=to-92]
  Q2 = NPN-Transistor [part_number=2N2222 package="TO92 [THT]"]
  LED1 = Super Flux LED blue [color=Blue]
  BAT1 = Battery Holders [package=battery-aa]

nets:
  N1: R1.Pin_0, C1.2
  N2: R1.Pin_1, R2.Pin_0, Q1.B
  N3: R2.Pin_1, S1.2, Q2.E
  N4: C1.1, Q1.E, Q2.C, LED1.anode, LED1.cathode, BAT1.+
  N5: S1.1, BAT1.-
  N6: Q1.C, Q2.B
